# Fritzing sketch for uploading sketch directly to ESP8266 (saved by Fritzing 0.9.3b)
breadboards: 2

parts:
  U2 = ESP8266 WiFi Module [part_number=ESP8266]
  Part1 = Arduino Nano (Rev3.0)
  R1 = Resistor [tolerance=±5% resistance=100k package=THT]
  U3 = ESP8266 WiFi Module [part_number=ESP8266]  # not connected

nets:
  N1: U2.RXD, Part1.D0/RX
  VCC: U2.VCC, Part1.3V3, R1.Pin_0
  GND: U2.GPIO_0, U2.GND, Part1.GND, Part1.RESET
  N2: U2.CH_PD, R1.Pin_1
  N3: U2.TXD, Part1.D1/TX

notes:
  To upload code to ESP8266
  Reset on nano puts into pass through mode.
  CHPD on ESP8266 must be set high to turn it on.
  GPIO0 to ground to put it in upload mode.
  RX to RX
  TX to TX
  note: between uploads you may have to unplug the nano from the computer.

custom parts:
  ESP8266 WiFi Module: Generic WiFi Module based on the ESP8266 with onboard PCB antenna and UART communications
